# Fritzing sketch Sketch 2 (saved by Fritzing 0.9.3b)

parts:
  Part1 = Arduino Mega 2560 (Rev3)
  hc-sr1 = hc-sr04
  hc-sr2 = hc-sr04
  hc-sr3 = hc-sr04
  S1 = H-Bridge with L298N
  M1 = DC Motor
  M2 = DC Motor
  VCC1 = 4 x AAA Battery Mount

nets:
  N1: Part1.D13_PWM, S1.ENA
  N2: Part1.D12_PWM, S1.IN1
  N3: Part1.D11_PWM, S1.IN2
  N4: Part1.D10_PWM, S1.IN3
  N5: Part1.D9_PWM, S1.IN4
  N6: Part1.D8_PWM, S1.ENB
  VCC: Part1.5V, hc-sr1.VCC, hc-sr2.VCC, hc-sr3.VCC
  GND: Part1.GND, hc-sr1.GND, hc-sr2.GND, hc-sr3.GND, S1.GND, VCC1.-
  VIN: Part1.VIN, S1.5V
  N7: Part1.D2_PWM, hc-sr1.Echo
  N8: Part1.D3_PWM, hc-sr1.Trig
  N9: Part1.D4_PWM, hc-sr3.Echo
  N10: Part1.D5_PWM, hc-sr3.Trig
  N11: Part1.D6_PWM, hc-sr2.Echo
  N12: Part1.D7_PWM, hc-sr2.Trig
  N13: S1.12V, VCC1.+
  N14: S1.M1-01, M2.pin_2
  N15: S1.M1-02, M2.pin_1
  N16: S1.M2-01, M1.pin_2
  N17: S1.M2-02, M1.pin_1

custom parts:
  H-Bridge with L298N: h-bridge
